// Digital circuit Full_Adder.dig as structural Verilog
module Full_Adder (
  input  Ai,
  input  Bi,
  input  Ci,
  output Co,
  output S
);

  wire and_1_out, and_2_out, and_3_out, and_4_out, and_5_out, and_6_out, not_1_out, not_2_out, not_3_out,
       not_4_out, or_1_out;

  and and_1 (and_1_out, Ai, Bi);
  not not_1 (not_1_out, Ai);
  not not_2 (not_2_out, Bi);
  and and_2 (and_2_out, not_1_out, Bi);
  and and_3 (and_3_out, Ai, not_2_out);
  or or_1 (or_1_out, and_2_out, and_3_out);
  and and_4 (and_4_out, or_1_out, Ci);
  not not_3 (not_3_out, or_1_out);
  not not_4 (not_4_out, Ci);
  or or_2 (Co, and_1_out, and_4_out);
  and and_5 (and_5_out, not_3_out, Ci);
  and and_6 (and_6_out, or_1_out, not_4_out);
  or or_3 (S, and_5_out, and_6_out);

  // Notes on the sheet:
  //   xor
endmodule
